// Logisim project broken-datapath.circ as structural Verilog: 3 circuits, main circuit main
module main (
  input  RegWrite,
  input  MemtoReg,
  input  MemWrite,
  input  MemRead,
  input  [1:0] ALUOp,
  output Zero,
  output halt
);

  wire clk, RegWirte;
  wire [31:0] adder_1_out, alu_1_result, data_memory_1_p6, instruction_memory_1_p2, multiplexer_1_out, pc,
       regfile_1_rd1, regfile_1_rd2;

  Clock clock_1 (.out(clk));
  Adder #(.width(32)) adder_1 (.a(pc), .b(32'h4), .out(adder_1_out));  // open: cin, cout
  Register #(.width(32)) u_PC (.D(adder_1_out), .Q(pc));  // open: en, clk, clr
  Comparator #(.width(32)) comparator_1 (.a(pc), .b(32'h10), .eq(halt));  // open: gt, lt
  // Instruction_Memory instruction_memory_1: pin names not known; wires that end beside it: pc, instruction_memory_1_p2
  regfile regfile_1 (
    .RR1(instruction_memory_1_p2[25:21]), .RR2(instruction_memory_1_p2[20:16]),
    .WR(instruction_memory_1_p2[15:11]), .WD(multiplexer_1_out), .RegWrite(RegWirte), .clk(clk),
    .RD1(regfile_1_rd1), .RD2(regfile_1_rd2));
  alu alu_1 (.A(regfile_1_rd1), .B(regfile_1_rd2), .ALUOp(ALUOp), .Result(alu_1_result), .Zero(Zero));
  // Data_Memory data_memory_1: pin names not known; wires that end beside it: alu_1_result, regfile_1_rd2, clk, MemWrite, MemRead, data_memory_1_p6
  Multiplexer #(.width(32), .enable("false")) multiplexer_1 (
    .in0(alu_1_result), .in1(data_memory_1_p6), .out(multiplexer_1_out), .sel(MemtoReg));
endmodule

module regfile (
  input  [4:0] RR1,
  input  [4:0] RR2,
  input  [4:0] WR,
  input  [31:0] WD,
  input  RegWrite,
  input  clk,
  output [31:0] RD1,
  output [31:0] RD2
);

  wire sel1, sel2, sel3, we1, we2, we3;
  wire [31:0] r1, r2, r3;

  Decoder #(.select(2), .enable("false")) decoder_1 (
    .out1(sel1), .out2(sel2), .out3(sel3), .sel(WR[1:0]));  // open: out0
  and and_1 (we1, sel1, RegWrite);
  and and_2 (we2, sel2, RegWrite);
  and and_3 (we3, sel3, RegWrite);
  Register #(.width(32)) _1 (.D(WD), .en(we1), .Q(r1), .clk(clk));  // open: clr
  Register #(.width(32)) _2 (.D(WD), .en(we2), .Q(r2), .clk(clk));  // open: clr
  Register #(.width(32)) _3 (.D(WD), .en(we3), .Q(r3), .clk(clk));  // open: clr
  Multiplexer #(.select(2), .width(32), .enable("false")) multiplexer_1 (
    .in0({32{1'b0}}), .in1(r1), .in2(r2), .in3(r3), .out(RD1), .sel(RR1[1:0]));
  Multiplexer #(.select(2), .width(32), .enable("false")) multiplexer_2 (
    .in0({32{1'b0}}), .in1(r1), .in2(r2), .in3(r3), .out(RD2), .sel(RR2[1:0]));

  // Other names for the same wires on the sheet: RR1lo[1:0] = RR1[1:0]; RR2lo[1:0] = RR2[1:0]; WRlo[1:0] = WR[1:0]
endmodule

module alu (
  input  [31:0] A,
  input  [31:0] B,
  input  [1:0] ALUOp,
  output [31:0] Result,
  output Zero
);

  wire [31:0] andv, diff, orv, sum;

  Adder #(.width(32)) adder_1 (.a(A), .b(B), .out(sum));  // open: cin, cout
  Subtractor #(.width(32)) subtractor_1 (.a(A), .b(B), .out(diff));  // open: bin, bout
  assign andv = A & B;  // AND_Gate and_1, 32 bits wide
  assign orv = A | B;  // OR_Gate or_1, 32 bits wide
  Multiplexer #(.select(2), .width(32), .enable("false")) multiplexer_1 (
    .in0(sum), .in1(diff), .in2(andv), .in3(orv), .out(Result), .sel(ALUOp));
  Comparator #(.width(32)) comparator_1 (.a(Result), .b({32{1'b0}}), .eq(Zero));  // open: gt, lt
endmodule
