// Logisim project two-imems.circ as structural Verilog: 1 circuit, main circuit main
module main (
);

  // Instruction_Memory IM1: pin names not known
  // Instruction_Memory IM2: pin names not known
  // Data_Memory data_memory_1: pin names not known
endmodule
