// Logisim project console-demo.circ as structural Verilog: 1 circuit, main circuit main
module main (
);

  wire clk, done;
  wire [31:0] A0, count, V0;

  Clock clock_1 (.out(clk));
  Counter #(.width(32), .max('hffffffff)) u_count (.Q(count), .clk(clk));  // open: load, D, count, carry, clr
  Adder #(.width(32)) adder_1 (.a(32'h41), .b(count), .out(A0));  // open: cin, cout
  Comparator #(.width(32)) comparator_1 (.a(count), .b(32'h6), .eq(done));  // open: gt, lt
  Multiplexer #(.width(32), .enable("false")) multiplexer_1 (.in0(32'hb), .in1(32'ha), .out(V0), .sel(done));
  // Console out: pin names not known; wires that end beside it: clk
endmodule
