// Logisim project counter-4bit.circ as structural Verilog: 1 circuit, main circuit main
module main (
  output [3:0] Q
);

  wire clock_1_out;
  wire [3:0] adder_1_out;

  Clock clock_1 (.out(clock_1_out));
  Register #(.width(4)) count (.D(adder_1_out), .Q(Q), .clk(clock_1_out));  // open: en, clr
  Adder #(.width(4)) adder_1 (.a(Q), .b(4'b0001), .out(adder_1_out));  // open: cin, cout
endmodule
