// Logisim project dynamic-e-conflict.circ as structural Verilog: 1 circuit, main circuit main
module main (
  output y
);

  wire clk, w;

  Clock clock_1 (.out(clk));
  assign w = clk ? 1'b0 : 1'bz;  // Controlled_Buffer controlled_buffer_1
  not not_1 (y, w);
  // also tied to VCC on the sheet: w
endmodule
