// Logisim project dynamic-e-undefined-input.circ as structural Verilog: 1 circuit, main circuit main
module main (
  input  RegWrite,
  output we
);

  wire clk;

  Clock clock_1 (.out(clk));
  and and_1 (we, RegWrite, clk);
endmodule
