// Logisim project dynamic-oscillation.circ as structural Verilog: 1 circuit, main circuit main
module main (
  output q
);

  wire clk;

  Clock clock_1 (.out(clk));
  nand nand_1 (q, clk, q);
endmodule
