// Logisim project dynamic-x-write-control.circ as structural Verilog: 1 circuit, main circuit main
module main (
  input  RegWrite,
  output [7:0] q
);

  wire clk;

  Clock clock_1 (.out(clk));
  Register R1 (.D(8'h7), .en(RegWrite), .Q(q), .clk(clk));  // open: clr
endmodule
