// Logisim project dynamic-x-write-data.circ as structural Verilog: 1 circuit, main circuit main
module main (
  input  [7:0] next,
  output [7:0] q
);

  wire clk;

  Clock clock_1 (.out(clk));
  Register PC (.D(next), .Q(q), .clk(clk));  // open: en, clr
endmodule
