// Logisim project mips-console-syscall.circ as structural Verilog: 1 circuit, main circuit main
module main (
);

  wire clk;

  Clock clock_1 (.out(clk));
  // Console console_1: pin names not known; wires that end beside it: clk
endmodule
