// Logisim project static-clock-unconnected.circ as structural Verilog: 1 circuit, main circuit main
module main (
  output [7:0] q
);

  Register PC (.D(8'h4), .Q(q));  // open: en, clk, clr
endmodule
