// Logisim project static-input-unconnected.circ as structural Verilog: 1 circuit, main circuit main
module main (
  output [7:0] s
);

  Adder adder_1 (.a(8'h1), .out(s));  // open: b, cin, cout
endmodule
