// Logisim project static-memory-overlap.circ as structural Verilog: 1 circuit, main circuit main
module main (
);

  wire clk;

  Clock clock_1 (.out(clk));
  // Data_Memory data_memory_1: pin names not known; wires that end beside it: 32'h10010000, 32'h10010000, clk, 1'b0, 1'b0
  // Stack stack_1: pin names not known; wires that end beside it: 32'h10010000, 32'h10010000, clk, 1'b0, 1'b0
endmodule
