// Logisim project static-subcircuit-port-unconnected.circ as structural Verilog: 2 circuits, main circuit main
module main (
  output y
);

  \buf  buf_1 (.Y(y));  // open: A
endmodule

module \buf  (
  input  A,
  output Y
);

  buf buffer_1 (Y, A);
endmodule
