// Logisim project static-tunnel-unpaired.circ as structural Verilog: 1 circuit, main circuit main
module main (
  output [4:0] w
);

  wire RegDest;

  Multiplexer #(.width(5), .enable("false")) multiplexer_1 (.in0(5'b00001), .in1(5'b00010), .out(w), .sel(RegDest));
endmodule
