// Logisim project static-width-mismatch.circ as structural Verilog: 1 circuit, main circuit main
module main (
  output [4:0] rs
);

  // Pins of 5 and 32 bits meet at 32'h1

  assign rs = 5'b00001;
endmodule
