// Logisim project gate-chain.circ as structural Verilog: 1 circuit, main circuit main
module main (
  input  A,
  input  B,
  input  C,
  output Y
);

  wire na, x;

  not n1 (na, A);
  and g1 (x, na, B);
  or g2 (Y, x, C);
endmodule
