// Logisim project loop.circ as structural Verilog: 1 circuit, main circuit main
module main (
  input  A,
  output Y
);

  wire back, x;

  or o (x, A, back);
  not nx (back, x);
  buf bf (Y, back);
endmodule
