// Logisim project mux.circ as structural Verilog: 1 circuit, main circuit main
module main (
  input  [3:0] A,
  input  [3:0] B,
  input  S,
  output [3:0] Y
);

  Multiplexer #(.width(4)) multiplexer_1 (.in0(A), .in1(B), .out(Y), .sel(S));  // open: en
endmodule
