// Logisim project register.circ as structural Verilog: 1 circuit, main circuit main
module main (
  input  A,
  output Y
);

  wire d, q;

  Clock clk ();  // open: out
  not n1 (d, A);
  Register #(.width(1)) R (.D(d), .Q(q));  // open: en, clk, clr
  not n2 (Y, q);
endmodule
