// Logisim project splitter.circ as structural Verilog: 1 circuit, main circuit main
module main (
  input  [31:0] Instruction,
  output [5:0] OP,
  output [4:0] LO,
  output [4:0] HI
);

  assign OP = ~Instruction[31:26];  // NOT_Gate nop, 6 bits wide
  assign LO = ~Instruction[25:21];  // NOT_Gate nlo, 5 bits wide
  assign HI = ~Instruction[20:16];  // NOT_Gate nhi, 5 bits wide

  // Other names for the same wires on the sheet: funct[5:0] = Instruction[5:0]; shamt[4:0] = Instruction[10:6];
  //   rd[4:0] = Instruction[15:11]; op_t[5:0] = Instruction[31:26]; lo_t[4:0] = Instruction[25:21];
  //   rs[4:0] = Instruction[25:21]; rsrt[9:0] = {Instruction[20:16], Instruction[25:21]};
  //   hi_t[4:0] = Instruction[20:16]; rt[4:0] = Instruction[20:16]
endmodule
