// Logisim project subcircuit.circ as structural Verilog: 2 circuits, main circuit main
module main (
  input  A,
  input  B,
  output Y,
  output Z
);

  blk blk_1 (.a(A), .b(B), .y(Y), .z(Z));
endmodule

module blk (
  input  a,
  input  b,
  output y,
  output z
);

  not ny (y, a);
  not nz (z, b);
endmodule
