// Logisim project gates.circ as structural Verilog: 1 circuit, main circuit main
module main (
  output [2:0] n,
  output \and ,
  output \or ,
  output \nand ,
  output \nor ,
  output halt,
  output \xnor ,
  output xor3,
  output notc,
  output mux
);

  wire clk;

  Clock clock_1 (.out(clk));
  Counter #(.width(3), .max('h7)) counter_1 (
    .load(1'b0), .count(1'b1), .Q(n), .carry(halt), .clk(clk), .clr(1'b0));  // open: D
  and and_1 (\and , n[0], n[1]);
  or or_1 (\or , n[0], n[1]);
  nand nand_1 (\nand , n[0], n[1]);
  nor nor_1 (\nor , n[0], n[1]);
  xnor xnor_1 (\xnor , n[0], n[1]);
  ExactlyOne xor_1 (.out(xor3), .in0(n[0]), .in1(n[1]), .in2(n[2]));
  not not_1 (notc, n[2]);
  Multiplexer #(.enable("false")) multiplexer_1 (.in0(n[0]), .in1(n[1]), .out(mux), .sel(n[2]));

  // Other names for the same wires on the sheet: a = n[0]; b = n[1]; c = n[2]
endmodule
