// Logisim project 1bit_adder.circ as structural Verilog: 1 circuit, main circuit 1bit_adder
module _1bit_adder (
  input  a,
  input  b,
  input  cin,
  output s,
  output cout
);

  wire ab, ac, bc;

  and and_1 (ab, a, b);
  and and_2 (ac, a, cin);
  and and_3 (bc, b, cin);
  xor xor_1 (s, a, b, cin);
  or or_1 (cout, ab, ac, bc);
endmodule
