// Logisim project adder_check.circ as structural Verilog: 1 circuit, main circuit main
module main (
  output [4:0] sum,
  output halt
);

  wire fa0_cout, fa1_cout, fa2_cout;

  _1bit_adder fa0 (.a(1'b1), .b(1'b0), .cin(1'b1), .cout(fa0_cout), .s(sum[0]));
  _1bit_adder fa1 (.a(1'b1), .b(1'b1), .cin(fa0_cout), .cout(fa1_cout), .s(sum[1]));
  _1bit_adder fa2 (.a(1'b0), .b(1'b1), .cin(fa1_cout), .cout(fa2_cout), .s(sum[2]));
  _1bit_adder fa3 (.a(1'b1), .b(1'b0), .cin(fa2_cout), .cout(sum[4]), .s(sum[3]));

  assign halt = 1'b1;

  // Other names for the same wires on the sheet: s0 = sum[0]; s1 = sum[1]; s2 = sum[2]; s3 = sum[3]; s4 = sum[4]
endmodule
