// Logisim project ripple_carry.circ as structural Verilog: 1 circuit, main circuit main
module main (
  input  cin,
  input  a0,
  input  b0,
  input  a1,
  input  b1,
  input  a2,
  input  b2,
  input  a3,
  input  b3,
  output s0,
  output s1,
  output s2,
  output s3,
  output cout
);

  wire fa0_cout, fa1_cout, fa2_cout;

  _1bit_adder fa0 (.a(a0), .b(b0), .cin(cin), .cout(fa0_cout), .s(s0));
  _1bit_adder fa1 (.a(a1), .b(b1), .cin(fa0_cout), .cout(fa1_cout), .s(s1));
  _1bit_adder fa2 (.a(a2), .b(b2), .cin(fa1_cout), .cout(fa2_cout), .s(s2));
  _1bit_adder fa3 (.a(a3), .b(b3), .cin(fa2_cout), .cout(cout), .s(s3));
endmodule
