// Logisim project ripple-carry-4bit.circ as structural Verilog: 2 circuits, main circuit main
module main (
  input  Cin,
  input  A0,
  input  B0,
  input  A1,
  input  B1,
  input  A2,
  input  B2,
  input  A3,
  input  B3,
  output S0,
  output S1,
  output S2,
  output S3,
  output Cout
);

  wire FA0_cout, FA1_cout, FA2_cout;

  full_adder FA0 (.A(A0), .B(B0), .Cin(Cin), .S(S0), .Cout(FA0_cout));
  full_adder FA1 (.A(A1), .B(B1), .Cin(FA0_cout), .S(S1), .Cout(FA1_cout));
  full_adder FA2 (.A(A2), .B(B2), .Cin(FA1_cout), .S(S2), .Cout(FA2_cout));
  full_adder FA3 (.A(A3), .B(B3), .Cin(FA2_cout), .S(S3), .Cout(Cout));
endmodule

module full_adder (
  input  A,
  input  B,
  input  Cin,
  output S,
  output Cout
);

  wire and_1_out, and_2_out, xor_1_out;

  xor xor_1 (xor_1_out, A, B);
  and and_1 (and_1_out, A, B);
  xor xor_2 (S, xor_1_out, Cin);
  and and_2 (and_2_out, xor_1_out, Cin);
  or or_1 (Cout, and_1_out, and_2_out);
endmodule
