// Logisim project stack-demo.circ as structural Verilog: 1 circuit, main circuit main
module main (
);

  wire clk;
  wire [31:0] count, next, offset, sp;

  Clock clock_1 (.out(clk));
  Counter #(.width(32), .max('hffffffff)) u_count (.Q(count), .clk(clk));  // open: load, D, count, carry, clr
  Shifter #(.width(32)) shifter_1 (.in(count), .\dist (5'b00010), .out(offset));
  Subtractor #(.width(32)) subtractor_1 (.a(32'h7fffeff8), .b(offset), .out(next));  // open: bin, bout
  Register #(.width(32)) u_sp (.D(next), .Q(sp), .clk(clk));  // open: en, clr
  // Data_Memory data_memory_1: pin names not known; wires that end beside it: next, count, clk, 1'b1, 1'b1
endmodule
