// Logisim project subcircuit.circ as structural Verilog: 2 circuits, main circuit main
module main (
  output [2:0] n,
  output sum,
  output cout,
  output halt
);

  wire c1, c2, clk, s1;

  Clock clock_1 (.out(clk));
  Counter #(.width(3), .max('h7)) counter_1 (
    .load(1'b0), .count(1'b1), .Q(n), .carry(halt), .clk(clk), .clr(1'b0));  // open: D
  half_adder half_adder_1 (.a(n[0]), .b(n[1]), .s(s1), .c(c1));
  half_adder half_adder_2 (.a(s1), .b(n[2]), .s(sum), .c(c2));
  or or_1 (cout, c1, c2);

  // Other names for the same wires on the sheet: a = n[0]; b = n[1]; cin = n[2]
endmodule

module half_adder (
  input  a,
  input  b,
  output s,
  output c
);

  xor xor_1 (s, a, b);
  and and_1 (c, a, b);
endmodule
