// Logisim project values.circ as structural Verilog: 1 circuit, main circuit main
module main (
  output short,
  output floating,
  output andfloat,
  output [3:0] partial,
  output [7:0] wired,
  output halt
);

  buf and_1 (andfloat, 1'b1);  // AND_Gate

  assign halt = 1'b1;
  assign partial[1:0] = 2'b10;
  assign short = 1'b1;
  assign wired = 8'ha5;
endmodule
