// Logisim project ref-mips.circ as structural Verilog: 1 circuit, main circuit main
module main (
  output [31:0] pc,
  output halt
);

  wire ALUSrc, Beq, Bne, clk, dec0, dec1, dec2, dec3, dec4, dec5, dec6, dec7, dec8, dec9, dec10, dec11,
       dec12, dec13, dec14, dec15, dec16, dec17, dec18, dec19, dec20, dec21, dec22, dec23, dec24, dec25,
       dec26, dec27, dec28, dec29, dec30, dec31, eq, neq, regimmCond, regWrite_t, rsSign, sltBit, sltuBit,
       take, tBeq, tBne, tRegimm, we1, we2, we3, we4, we5, we6, we7, we8, we9, we10, we11, we12, we13, we14,
       we15, we16, we17, we18, we19, we20, we21, we22, we23, we24, we25, we26, we27, we28, we29, we30, we31,
       write;
  wire [4:0] \dist , rs5, writeReg;
  wire [7:0] aluctl;
  wire [9:0] aluAddr;
  wire [15:6] imm;
  wire [16:0] ctrl;
  wire [25:0] rsMid;
  wire [31:0] addv, aluB, aluResult, andv, btarget, immExt, immS, immZ, memData, mulv, n1, n2, norv, npc,
       npcx, off, orv, pc4, pcx, r1, r2, r3, r4, r5, r6, r7, r8, r9, r10, r11, r12, r13, r14, r15, r16, r17,
       r18, r19, r20, r21, r22, r23, r24, r25, r26, r27, r28, r29, r30, r31, rtVal, sllv, sltuv, sltv, srav,
       srlv, subv, writeData, xorv;
  wire [31:16] instr;

  Clock clock_1 (.out(clk));
  Subtractor #(.width(32)) subtractor_1 (.a({rsSign, rsMid, rs5}), .b(aluB), .out(subv));  // open: bin, bout
  Shifter #(.width(32), .shift("lr")) shifter_1 (.in(rtVal), .\dist (\dist ), .out(srlv));
  Decoder #(.select(5), .enable("false")) decoder_1 (
    .out0(dec0), .out1(dec1), .out2(dec2), .out3(dec3), .out4(dec4), .out5(dec5), .out6(dec6), .out7(dec7),
    .out8(dec8), .out9(dec9), .out10(dec10), .out11(dec11), .out12(dec12), .out13(dec13), .out14(dec14),
    .out15(dec15), .out16(dec16), .out17(dec17), .out18(dec18), .out19(dec19), .out20(dec20), .out21(dec21),
    .out22(dec22), .out23(dec23), .out24(dec24), .out25(dec25), .out26(dec26), .out27(dec27), .out28(dec28),
    .out29(dec29), .out30(dec30), .out31(dec31), .sel(writeReg));
  and and_1 (we6, dec6, regWrite_t);
  and and_2 (we12, dec12, regWrite_t);
  and and_3 (we18, dec18, regWrite_t);
  and and_4 (we24, dec24, regWrite_t);
  and and_5 (we30, dec30, regWrite_t);
  and and_6 (tBne, Bne, neq);
  Multiplexer #(.width(32), .enable("false")) multiplexer_1 (
    .in0(n1), .in1({pc[31:28], instr[25:16], imm, aluAddr[5:0], 2'b00}), .out(n2), .sel(ctrl[10]));
  assign andv = {rsSign, rsMid, rs5} & aluB;  // AND_Gate and_7, 32 bits wide
  Shifter #(.width(32), .shift("ar")) shifter_2 (.in(rtVal), .\dist (\dist ), .out(srav));
  Register #(.width(32)) _6 (.D(writeData), .en(we6), .Q(r6), .clk(clk), .clr(1'b0));
  Register #(.width(32)) _12 (.D(writeData), .en(we12), .Q(r12), .clk(clk), .clr(1'b0));
  Register #(.width(32)) _18 (.D(writeData), .en(we18), .Q(r18), .clk(clk), .clr(1'b0));
  Register #(.width(32)) _24 (.D(writeData), .en(we24), .Q(r24), .clk(clk), .clr(1'b0));
  Register #(.width(32)) _30 (.D(writeData), .en(we30), .Q(r30), .clk(clk), .clr(1'b0));
  Multiplexer #(.width(32), .enable("false")) multiplexer_2 (
    .in0(n2), .in1({rsSign, rsMid, rs5}), .out(npc), .sel(aluctl[5]));
  ROM #(.addrWidth(6), .dataWidth(17)) rom_1 (
    .addr(instr[31:26]),
    .data({ctrl[16], aluAddr[9], ctrl[14], aluAddr[8:6], ctrl[10], Bne, Beq, ctrl[7:3], ALUSrc, ctrl[1:0]}),
    .sel(1'b1));
  assign orv = {rsSign, rsMid, rs5} | aluB;  // OR_Gate or_1, 32 bits wide
  Multiplier #(.width(32)) multiplier_1 (.a({rsSign, rsMid, rs5}), .b(rtVal), .out(mulv));  // open: cin, cout
  and and_8 (we1, dec1, regWrite_t);
  and and_9 (we7, dec7, regWrite_t);
  and and_10 (we13, dec13, regWrite_t);
  and and_11 (we19, dec19, regWrite_t);
  and and_12 (we25, dec25, regWrite_t);
  and and_13 (we31, dec31, regWrite_t);
  xor xor_1 (regimmCond, instr[16], rsSign);
  assign xorv = {rsSign, rsMid, rs5} ^ aluB;  // XOR_Gate xor_2, 32 bits wide
  Multiplexer #(.select(4), .width(32), .enable("false")) multiplexer_3 (
    .in0(addv), .in1(subv), .in2(andv), .in3(orv), .in4(xorv), .in5(norv), .in6(sltv), .in7(sltuv),
    .in8(sllv), .in9(srlv), .in10(srav), .in11(mulv), .in12({32{1'b0}}), .in13({32{1'b0}}),
    .in14({32{1'b0}}), .in15({32{1'b0}}), .out(aluResult), .sel(aluctl[3:0]));
  Register #(.width(32)) _1 (.D(writeData), .en(we1), .Q(r1), .clk(clk), .clr(1'b0));
  Register #(.width(32)) _7 (.D(writeData), .en(we7), .Q(r7), .clk(clk), .clr(1'b0));
  Register #(.width(32)) _13 (.D(writeData), .en(we13), .Q(r13), .clk(clk), .clr(1'b0));
  Register #(.width(32)) _19 (.D(writeData), .en(we19), .Q(r19), .clk(clk), .clr(1'b0));
  Register #(.width(32)) _25 (.D(writeData), .en(we25), .Q(r25), .clk(clk), .clr(1'b0));
  Register #(.width(32)) _31 (.D(writeData), .en(we31), .Q(r31), .clk(clk), .clr(1'b0));
  and and_14 (tRegimm, ctrl[16], regimmCond);
  Register #(.width(32)) register_1 (.D(npcx), .en(1'b1), .Q(pcx), .clk(clk), .clr(1'b0));
  assign norv = ~({rsSign, rsMid, rs5} | aluB);  // NOR_Gate nor_1, 32 bits wide
  and and_15 (we2, dec2, regWrite_t);
  and and_16 (we8, dec8, regWrite_t);
  and and_17 (we14, dec14, regWrite_t);
  and and_18 (we20, dec20, regWrite_t);
  and and_19 (we26, dec26, regWrite_t);
  Multiplexer #(.select(5), .width(32), .enable("false")) multiplexer_4 (
    .in0({32{1'b0}}), .in1(r1), .in2(r2), .in3(r3), .in4(r4), .in5(r5), .in6(r6), .in7(r7), .in8(r8),
    .in9(r9), .in10(r10), .in11(r11), .in12(r12), .in13(r13), .in14(r14), .in15(r15), .in16(r16), .in17(r17),
    .in18(r18), .in19(r19), .in20(r20), .in21(r21), .in22(r22), .in23(r23), .in24(r24), .in25(r25),
    .in26(r26), .in27(r27), .in28(r28), .in29(r29), .in30(r30), .in31(r31), .out({rsSign, rsMid, rs5}),
    .sel(instr[25:21]));
  or or_2 (take, tBeq, tBne, tRegimm);
  ROM #(.addrWidth(10)) rom_2 (.addr(aluAddr), .data(aluctl), .sel(1'b1));
  Comparator #(.width(32)) comparator_1 (.a({rsSign, rsMid, rs5}), .b(aluB), .lt(sltBit));  // open: gt, eq
  Register #(.width(32)) _2 (.D(writeData), .en(we2), .Q(r2), .clk(clk), .clr(1'b0));
  Register #(.width(32)) _8 (.D(writeData), .en(we8), .Q(r8), .clk(clk), .clr(1'b0));
  Register #(.width(32)) _14 (.D(writeData), .en(we14), .Q(r14), .clk(clk), .clr(1'b0));
  Register #(.width(32)) _20 (.D(writeData), .en(we20), .Q(r20), .clk(clk), .clr(1'b0));
  Register #(.width(32)) _26 (.D(writeData), .en(we26), .Q(r26), .clk(clk), .clr(1'b0));
  Multiplexer #(.select(5), .width(32), .enable("false")) multiplexer_5 (
    .in0({32{1'b0}}), .in1(r1), .in2(r2), .in3(r3), .in4(r4), .in5(r5), .in6(r6), .in7(r7), .in8(r8),
    .in9(r9), .in10(r10), .in11(r11), .in12(r12), .in13(r13), .in14(r14), .in15(r15), .in16(r16), .in17(r17),
    .in18(r18), .in19(r19), .in20(r20), .in21(r21), .in22(r22), .in23(r23), .in24(r24), .in25(r25),
    .in26(r26), .in27(r27), .in28(r28), .in29(r29), .in30(r30), .in31(r31), .out(rtVal), .sel(instr[20:16]));
  assign pc = pcx ^ 32'h400024;  // XOR_Gate xor_3, 32 bits wide
  assign sltv = {{31{1'b0}}, sltBit};  // Bit_Extender bit_extender_1
  Multiplexer #(.select(2), .width(5), .enable("false")) multiplexer_6 (
    .in0(instr[20:16]), .in1(imm[15:11]), .in2({5{1'b1}}), .in3({5{1'b0}}), .out(writeReg), .sel(ctrl[1:0]));
  and and_20 (we3, dec3, regWrite_t);
  and and_21 (we9, dec9, regWrite_t);
  and and_22 (we15, dec15, regWrite_t);
  and and_23 (we21, dec21, regWrite_t);
  and and_24 (we27, dec27, regWrite_t);
  // Data_Memory data_memory_1: pin names not known; wires that end beside it: aluResult, rtVal, clk, ctrl[7], ctrl[6], memData
  Shifter #(.width(32)) shifter_3 (.in(immS), .\dist (5'b00010), .out(off));
  assign npcx = npc ^ 32'h400024;  // XOR_Gate xor_4, 32 bits wide
  assign immS = {{16{imm[15]}}, {imm, aluAddr[5:0]}};  // Bit_Extender bit_extender_2
  Comparator #(.width(32), .mode("unsigned")) comparator_2 (
    .a({rsSign, rsMid, rs5}), .b(aluB), .lt(sltuBit));  // open: gt, eq
  Register #(.width(32)) _3 (.D(writeData), .en(we3), .Q(r3), .clk(clk), .clr(1'b0));
  Register #(.width(32)) _9 (.D(writeData), .en(we9), .Q(r9), .clk(clk), .clr(1'b0));
  Register #(.width(32)) _15 (.D(writeData), .en(we15), .Q(r15), .clk(clk), .clr(1'b0));
  Register #(.width(32)) _21 (.D(writeData), .en(we21), .Q(r21), .clk(clk), .clr(1'b0));
  Register #(.width(32)) _27 (.D(writeData), .en(we27), .Q(r27), .clk(clk), .clr(1'b0));
  // Stack stack_1: pin names not known; wires that end beside it: aluResult, rtVal, clk, ctrl[7], ctrl[6], memData
  Adder #(.width(32)) adder_1 (.a(pc), .b(off), .out(btarget));  // open: cin, cout
  assign immZ = {{16{1'b0}}, {imm, aluAddr[5:0]}};  // Bit_Extender bit_extender_3
  assign sltuv = {{31{1'b0}}, sltuBit};  // Bit_Extender bit_extender_4
  and and_25 (we4, dec4, regWrite_t);
  and and_26 (we10, dec10, regWrite_t);
  and and_27 (we16, dec16, regWrite_t);
  and and_28 (we22, dec22, regWrite_t);
  and and_29 (we28, dec28, regWrite_t);
  // Console console_1: pin names not known; wires that end beside it: clk, halt
  Adder #(.width(32)) adder_2 (.a(pc), .b(32'h4), .out(pc4));  // open: cin, cout
  Multiplexer #(.width(32), .enable("false")) multiplexer_7 (.in0(immS), .in1(immZ), .out(immExt), .sel(ctrl[14]));
  Multiplexer #(.select(2), .width(32), .enable("false")) multiplexer_8 (
    .in0(aluResult), .in1(memData), .in2(pc4), .in3({imm, aluAddr[5:0], {16{1'b0}}}), .out(writeData),
    .sel(ctrl[4:3]));
  Register #(.width(32)) _4 (.D(writeData), .en(we4), .Q(r4), .clk(clk), .clr(1'b0));
  Register #(.width(32)) _10 (.D(writeData), .en(we10), .Q(r10), .clk(clk), .clr(1'b0));
  Register #(.width(32)) _16 (.D(writeData), .en(we16), .Q(r16), .clk(clk), .clr(1'b0));
  Register #(.width(32)) _22 (.D(writeData), .en(we22), .Q(r22), .clk(clk), .clr(1'b0));
  Register #(.width(32)) _28 (.D(writeData), .en(we28), .Q(r28), .clk(clk), .clr(1'b0));
  Comparator #(.width(32)) comparator_3 (.a({rsSign, rsMid, rs5}), .b(rtVal), .eq(eq));  // open: gt, lt
  // Instruction_Memory instruction_memory_1: pin names not known; wires that end beside it: pc, {instr, imm, aluAddr[5:0]}
  Multiplexer #(.width(32), .enable("false")) multiplexer_9 (.in0(rtVal), .in1(immExt), .out(aluB), .sel(ALUSrc));
  Multiplexer #(.width(5), .enable("false")) multiplexer_10 (.in0(imm[10:6]), .in1(rs5), .out(\dist ), .sel(aluctl[4]));
  not not_1 (write, aluctl[7]);
  and and_30 (we5, dec5, regWrite_t);
  and and_31 (we11, dec11, regWrite_t);
  and and_32 (we17, dec17, regWrite_t);
  and and_33 (we23, dec23, regWrite_t);
  and and_34 (we29, dec29, regWrite_t);
  not not_2 (neq, eq);
  Adder #(.width(32)) adder_3 (.a({rsSign, rsMid, rs5}), .b(aluB), .out(addv));  // open: cin, cout
  Shifter #(.width(32)) shifter_4 (.in(rtVal), .\dist (\dist ), .out(sllv));
  and and_35 (regWrite_t, ctrl[5], write);
  Register #(.width(32)) _5 (.D(writeData), .en(we5), .Q(r5), .clk(clk), .clr(1'b0));
  Register #(.width(32)) _11 (.D(writeData), .en(we11), .Q(r11), .clk(clk), .clr(1'b0));
  Register #(.width(32)) _17 (.D(writeData), .en(we17), .Q(r17), .clk(clk), .clr(1'b0));
  Register #(.width(32)) _23 (.D(writeData), .en(we23), .Q(r23), .clk(clk), .clr(1'b0));
  Register #(.width(32)) _29 (.D(writeData), .en(we29), .Q(r29), .clk(clk), .clr(1'b0));
  and and_36 (tBeq, Beq, eq);
  Multiplexer #(.width(32), .enable("false")) multiplexer_11 (.in0(pc4), .in1(btarget), .out(n1), .sel(take));

  // Other names for the same wires on the sheet: ALUOp[2:0] = aluAddr[8:6];
  //   ctrl (some bits) = {aluAddr[9:6], Bne, Beq, ALUSrc}; Special2 = aluAddr[9]; ALUFunc[3:0] = aluctl[3:0];
  //   ShiftVar = aluctl[4]; JR = aluctl[5]; Syscall = aluctl[6]; NoWrite = aluctl[7]; RegDst[1:0] = ctrl[1:0];
  //   MemtoReg[1:0] = ctrl[4:3]; RegWrite = ctrl[5]; MemRead = ctrl[6]; MemWrite = ctrl[7]; Jump = ctrl[10];
  //   ZeroExt = ctrl[14]; Regimm = ctrl[16]; instrHi[15:0] = instr; instrOp[5:0] = instr[31:26];
  //   op[5:0] = instr[31:26]; funct[5:0] = aluAddr[5:0]; imm[5:0] = aluAddr[5:0]; instr[15:0] = {imm, aluAddr[5:0]};
  //   jtarget[31:2] = {pc[31:28], instr[25:16], imm, aluAddr[5:0]}; luiv[31:16] = {imm, aluAddr[5:0]};
  //   target[25:0] = {instr[25:16], imm, aluAddr[5:0]}; shamt[4:0] = imm[10:6]; rd[4:0] = imm[15:11];
  //   rt[4:0] = instr[20:16]; rtBit0 = instr[16]; rtHi[3:0] = instr[20:17]; rs[4:0] = instr[25:21];
  //   pcTop[3:0] = pc[31:28]; pcLo[27:0] = pc[27:0]; rsVal[31:0] = {rsSign, rsMid, rs5}

  // Notes on the sheet:
  //   contents of rom_1 (hex, n*v repeats v):
  //   1021 10000 400 432 900 a00 0 0 24 24 3024 3824 5824 6024 6824 38 12*0 9021 6*0 6c 7*0 84
  //   contents of rom_2 (hex, n*v repeats v):
  //   64*0 64*1 8 80 9 a 18 80 19 1a a0 80 80 80 c0 19*80 0 0 1 1 2 3 4 5 80 80 6 7 20*80 64*2 64*3 64*4
  //   64*6 64*7 80 80 b 63*80 b 63*80 b 63*80 b 63*80 b 63*80 b 63*80 b 63*80 b 61*80
endmodule
