// Logisim project 01-place-parts.circ as structural Verilog: 1 circuit, main circuit main
module main (
  input  [7:0] A,
  input  [7:0] B,
  output [15:0] Y
);

  Clock clock_1 ();  // open: out
  // AND_Gate and_1 is placed but not wired
  // OR_Gate or_1 is placed but not wired
  // XOR_Gate xor_1 is placed but not wired
  // NAND_Gate nand_1 is placed but not wired
  // AND_Gate and_2 is placed but not wired
  // NOT_Gate not_1 is placed but not wired
  Multiplexer #(.select(2), .width(8)) multiplexer_1 ();  // open: in0, in1, in2, in3, out, sel, en
  Adder adder_1 ();  // open: a, b, out, cin, cout
  Register #(.width(16)) PC ();  // open: D, en, Q, clk, clr
  // Probe on nothing
endmodule
