// Logisim project 02-wires.circ as structural Verilog: 1 circuit, main circuit main
module main (
  output out_1
);

  wire undriven, undriven_2, undriven_3;

  and and_1 (out_1, undriven_3, undriven_3, undriven_3);
  // OR_Gate or_1 has open pins: in0=undriven, out=open
  // AND_Gate and_2 has open pins: in0=undriven_2, out=open
endmodule
