// Logisim project 03-move-following.circ as structural Verilog: 1 circuit, main circuit main
module main (
  input  a,
  input  b,
  input  c,
  input  d,
  output y
);

  wire undriven;

  // NOT_Gate not_1 has open pins: in=c, out=open
  and and_1 (y, undriven, b);
  // NOT_Gate not_2 is placed but not wired
endmodule
