// Logisim project 04-segment-delete.circ as structural Verilog: 1 circuit, main circuit main
module main (
  input  in,
  output out
);

  // NOT_Gate not_1 is placed but not wired
  // NOT_Gate not_2 is placed but not wired

  assign out = in;
endmodule
