// Logisim project 05-copy-paste-duplicate.circ as structural Verilog: 1 circuit, main circuit main
module main (
  input  x0,
  input  x0_2,
  input  x0_3
);

  wire not_1_out, not_2_out, not_3_out;

  // NOT_Gate not_1 has open pins: in=open, out=not_1_out
  // NOT_Gate not_2 has open pins: in=open, out=not_2_out
  // NOT_Gate not_3 has open pins: in=open, out=not_3_out
  // NOT_Gate not_4 is placed but not wired
  // AND_Gate and_1 has open pins: in0=not_2_out, out=open
  // AND_Gate and_2 has open pins: in0=not_3_out, out=open
  // AND_Gate and_3 is placed but not wired
  Register #(.width(32)) R0 ();  // open: D, en, Q, clk, clr
  Register #(.width(32)) R1 ();  // open: D, en, Q, clk, clr
  Register #(.width(32)) R2 ();  // open: D, en, Q, clk, clr
  Register #(.width(32)) R3 ();  // open: D, en, Q, clk, clr
endmodule
