// Logisim project 06-align-distribute.circ as structural Verilog: 1 circuit, main circuit main
module main (
  input  p1,
  input  p2,
  input  [7:0] p3
);

  wire n5_out;

  // NOT_Gate n1 is placed but not wired
  // NOT_Gate n5 has open pins: in=open, out=n5_out
  // NOT_Gate n2 is placed but not wired
  Adder adder_1 ();  // open: a, b, out, cin, cout
  Subtractor subtractor_1 ();  // open: a, b, out, bin, bout
  Register \reg  ();  // open: D, en, Q, clk, clr
  // NOT_Gate n3 is placed but not wired
  // NOT_Gate n4 is placed but not wired
endmodule
