// Logisim project 07-attributes.circ as structural Verilog: 1 circuit, main circuit top
// ALU
module top (
  input  [3:0] in_1,
  input  [3:0] sel,
  output [3:0] out_3
);

  wire undriven, undriven_2;

  // AND_Gate G1 is placed but not wired
  // OR_Gate or_1 has open pins: in0=undriven, in2=undriven_2, out=open
  Adder #(.width(16)) adder_1 ();  // open: a, b, out, cin, cout
  Multiplexer #(.select(3), .width(8)) multiplexer_1 ();  // open: in0, in1, in2, in3, in4, in5, in6, in7, out, sel, en
endmodule
