// Logisim project 08-subcircuit.circ as structural Verilog: 3 circuits, main circuit top
module main (
  input  x,
  input  y
);

  wire ha_1_p3;

  // ha ha_1: pin names not known; wires that end beside it: x, y, ha_1_p3
  ha ha_2 ();  // open: b, a, c, s
  ha ha_3 ();  // open: b, a, c, s
endmodule

module ha (
  input  a,
  input  b,
  output s,
  output c
);

  xor xor_1 (s, a, b);
  and and_1 (c, a, b);
endmodule

module top (
);

  main main_1 ();  // open: x, y
endmodule
