// Logisim project 09-import-subcircuits.circ as structural Verilog: 5 circuits, main circuit main
module main (
  output a
);

  full_adder full_adder_1 (.a(a));  // open: b, cin, s, cout
  parity3 parity3_1 ();  // open: x, p
endmodule

module half_adder (
);

  // NOT_Gate not_1 is placed but not wired
endmodule

module half_adder_2 (
  input  a,
  input  b,
  output s,
  output c
);

  xor xor_1 (s, a, b);
  and and_1 (c, a, b);
endmodule

module full_adder (
  input  a,
  input  b,
  input  cin,
  output s,
  output cout
);

  wire half_adder_2_1_c, half_adder_2_1_s, half_adder_2_2_c;

  half_adder_2 half_adder_2_1 (.a(a), .b(b), .s(half_adder_2_1_s), .c(half_adder_2_1_c));
  half_adder_2 half_adder_2_2 (.a(half_adder_2_1_s), .b(cin), .s(s), .c(half_adder_2_2_c));
  or or_1 (cout, half_adder_2_1_c, half_adder_2_2_c);
endmodule

module parity3 (
  input  x,
  output p
);

  buf xor_1 (p, x);  // XOR_Gate
endmodule
