// Logisim project 10-undo-redo.circ as structural Verilog: 1 circuit, main circuit main
module main (
);

  wire and_1_out;

  // AND_Gate and_1 has open pins: out=and_1_out
  // OR_Gate or_1 is placed but not wired
  // XOR_Gate xor_1 is placed but not wired
  // NOT_Gate not_1 is placed but not wired
  // NOT_Gate not_2 is placed but not wired
  // NAND_Gate nand_1 is placed but not wired
endmodule
