// Logisim project 11-load-libraries.circ as structural Verilog: 1 circuit, main circuit main
module main (
);

  wire full_adder_1_s;

  full_adder full_adder_1 (.s(full_adder_1_s));  // open: a, b, cin, cout
  // parity3 parity3_1: pin names not known
  LED led_1 ();  // open: in
  // Radix_Probe radix_probe_1: pin names not known; wires that end beside it: full_adder_1_s
  // Data_Memory data_memory_1: pin names not known
endmodule
