// Logisim project 12-mips-bundled.circ as structural Verilog: 1 circuit, main circuit main
module main (
);

  wire IMEM_p2;
  wire [31:0] PC_q;

  Register #(.width(32)) PC (.Q(PC_q));  // open: D, en, clk, clr
  // Instruction_Memory IMEM: pin names not known; wires that end beside it: PC_q, IMEM_p2
  // Radix_Probe radix_probe_1: pin names not known; wires that end beside it: IMEM_p2
  // Console console_1: pin names not known
  // Data_Memory DMEM: pin names not known
  // Stack stack_1: pin names not known
endmodule
