// Logisim project 15-zoom.circ as structural Verilog: 1 circuit, main circuit main
module main (
  input  in_1
);

  wire and_1_out;

  buf and_1 (and_1_out, in_1);  // AND_Gate
  // NOT_Gate not_1 is placed but not wired
endmodule
