// Logisim project 16-datapath-mix.circ as structural Verilog: 1 circuit, main circuit main
module main (
);

  wire clock_1_out;
  wire [31:0] adder_1_out, instruction_memory_1_p2, PC;

  Clock clock_1 (.out(clock_1_out));
  Register #(.width(32)) PC_reg (.D(adder_1_out), .Q(PC), .clk(clock_1_out));  // open: en, clr
  Adder #(.width(32)) adder_1 (.a(PC), .b(32'h4), .out(adder_1_out));  // open: cin, cout
  // Instruction_Memory instruction_memory_1: pin names not known; wires that end beside it: PC, instruction_memory_1_p2, instruction_memory_1_p2
endmodule
