// Logisim project 17-open-existing.circ as structural Verilog: 4 circuits, main circuit main
module main (
);

  full_adder full_adder_1 ();  // open: a, b, cin, s, cout
  odd3 odd3_1 ();  // open: p, p_2
endmodule

module half_adder (
  input  a,
  input  b,
  output sum,
  output c
);

  xor xor_1 (sum, a, b);
  and and_1 (c, a, b);
endmodule

module full_adder (
  input  a,
  input  b,
  input  cin,
  output s,
  output cout
);

  wire half_adder_1_c, half_adder_1_sum, half_adder_2_c;

  half_adder half_adder_1 (.a(a), .b(b), .sum(half_adder_1_sum), .c(half_adder_1_c));
  half_adder half_adder_2 (.a(half_adder_1_sum), .b(cin), .sum(s), .c(half_adder_2_c));
  // Probe on s
  or or_1 (cout, half_adder_1_c, half_adder_2_c);
endmodule

module odd3 (
  output p,
  output p_2
);

  wire undriven;

  buf xor_1 (p_2, undriven);  // XOR_Gate
endmodule
