// Logisim project adders.circ as structural Verilog
module half_adder (
  input  a,
  input  b,
  output s,
  output c
);

  xor xor_1 (s, a, b);
  and and_1 (c, a, b);
endmodule

module full_adder (
  input  a,
  input  b,
  input  cin,
  output s,
  output cout
);

  wire half_adder_1_c, half_adder_1_s, half_adder_2_c;

  half_adder half_adder_1 (.a(a), .b(b), .s(half_adder_1_s), .c(half_adder_1_c));
  half_adder half_adder_2 (.a(half_adder_1_s), .b(cin), .s(s), .c(half_adder_2_c));
  or or_1 (cout, half_adder_1_c, half_adder_2_c);
endmodule

module parity3 (
  input  x,
  output p
);

  buf xor_1 (p, x);  // XOR_Gate
endmodule
