// Logisim project tutorial-logic.circ as structural Verilog: 2 circuits, main circuit main
module main (
  input  A,
  input  B,
  input  P,
  input  Q,
  output Y
);

  wire clock_1_out;
  wire [3:0] adder_1_out, count_q;

  Adder #(.width(4)) adder_1 (.a(count_q), .b(4'b0001), .out(adder_1_out));  // open: cin, cout
  Clock clock_1 (.out(clock_1_out));
  Register #(.width(4)) count (.D(adder_1_out), .Q(count_q));  // open: en, clk, clr
  // Radix_Probe radix_probe_1: pin names not known; wires that end beside it: clock_1_out, count_q
  LED led_1 (.in(count_q[0]));
  LED led_2 (.in(count_q[1]));
  LED led_3 (.in(count_q[2]));
  LED led_4 (.in(count_q[3]));
endmodule

module half_adder (
  input  a,
  input  b,
  output s,
  output c
);

  xor xor_1 (s, a, b);
  and and_1 (c, a, b);
endmodule
