// Logisim project tutorial-mips.circ as structural Verilog: 4 circuits, main circuit main
module main (
);

  wire ALUSrc, Beq, Bne, clk, eq, exit, MemRead, MemWrite, ne, RegDst, RegWirte, RegWrite, running, started,
       Syscall, take, takeEq, takeNe, ZeroExt;
  wire [1:0] MemtoReg;
  wire [2:0] ALUCtl;
  wire [4:0] WR;
  wire [5:0] funct;
  wire [15:6] imm;
  wire [31:0] a0, aluB, aluResult, immExt, immS, immZ, memData, npc, offset, PC, pc4, PC_reg_q, rsVal, rtVal,
       target, v0, writeData;
  wire [31:16] instr;

  Clock clock_1 (.out(clk));
  not not_1 (running, exit);
  Register #(.width(32)) PC_reg (.D(npc), .en(running), .Q(PC_reg_q), .clk(clk));  // open: clr
  Register #(.width(1)) u_started (.D(1'b1), .Q(started), .clk(clk));  // open: en, clr
  Comparator #(.width(32)) comparator_1 (.a(rsVal), .b(rtVal), .eq(eq));  // open: gt, lt
  not not_2 (ne, eq);
  Shifter #(.width(32)) shifter_1 (.in(immS), .\dist (5'b00010), .out(offset));
  Multiplexer #(.width(32), .enable("false")) multiplexer_1 (.in0(32'h400000), .in1(PC_reg_q), .out(PC), .sel(started));
  and and_1 (takeEq, Beq, eq);
  and and_2 (takeNe, Bne, ne);
  Adder #(.width(32)) adder_1 (.a(PC), .b(offset), .out(target));  // open: cin, cout
  Adder #(.width(32)) adder_2 (.a(PC), .b(32'h4), .out(pc4));  // open: cin, cout
  // Instruction_Memory instruction_memory_1: pin names not known; wires that end beside it: PC, {instr, imm, funct}
  or or_1 (take, takeEq, takeNe);
  Multiplexer #(.width(32), .enable("false")) multiplexer_2 (.in0(pc4), .in1(target), .out(npc), .sel(take));
  Multiplexer #(.width(5), .enable("false")) multiplexer_3 (
    .in0(instr[20:16]), .in1(imm[15:11]), .out(WR), .sel(RegDst));
  assign immS = {{16{imm[15]}}, {imm, funct}};  // Bit_Extender bit_extender_1
  assign immZ = {{16{1'b0}}, {imm, funct}};  // Bit_Extender bit_extender_2
  control control_1 (
    .op(instr[31:26]), .funct(funct), .RegDst(RegDst), .ALUSrc(ALUSrc), .MemtoReg(MemtoReg),
    .RegWrite(RegWrite), .MemRead(MemRead), .MemWrite(MemWrite), .Beq(Beq), .Bne(Bne), .ZeroExt(ZeroExt),
    .ALUCtl(ALUCtl), .Syscall(Syscall));
  regfile regfile_1 (
    .RR1(instr[25:21]), .RR2(instr[20:16]), .WR(WR), .WD(writeData), .RegWrite(RegWirte), .clk(clk),
    .RD1(rsVal), .RD2(rtVal), .v0(v0), .a0(a0));
  Multiplexer #(.width(32), .enable("false")) multiplexer_4 (.in0(immS), .in1(immZ), .out(immExt), .sel(ZeroExt));
  Multiplexer #(.width(32), .enable("false")) multiplexer_5 (.in0(rtVal), .in1(immExt), .out(aluB), .sel(ALUSrc));
  alu alu_1 (.A(rsVal), .B(aluB), .ALUCtl(ALUCtl), .Result(aluResult));  // open: Zero
  // Data_Memory data_memory_1: pin names not known; wires that end beside it: aluResult, rtVal, clk, MemWrite, clk, MemRead, memData
  // Console console_1: pin names not known; wires that end beside it: exit
  Multiplexer #(.select(2), .width(32), .enable("false")) multiplexer_6 (
    .in0(aluResult), .in1(memData), .in2({imm, funct, {16{1'b0}}}), .in3({32{1'b0}}), .out(writeData),
    .sel(MemtoReg));

  // Other names for the same wires on the sheet: rt[4:0] = instr[20:16]; rs[4:0] = instr[25:21];
  //   op[5:0] = instr[31:26]; imm[5:0] = funct; instr[15:0] = {imm, funct}; luiv[31:16] = {imm, funct};
  //   shamt[4:0] = imm[10:6]; rd[4:0] = imm[15:11]
endmodule

module control (
  input  [5:0] op,
  input  [5:0] funct,
  output RegDst,
  output ALUSrc,
  output [1:0] MemtoReg,
  output RegWrite,
  output MemRead,
  output MemWrite,
  output Beq,
  output Bne,
  output ZeroExt,
  output [2:0] ALUCtl,
  output Syscall
);

  ROM #(.addrWidth(12), .dataWidth(14)) rom_1 (
    .addr({op, funct}),
    .data({Syscall, ALUCtl, ZeroExt, Bne, Beq, MemWrite, MemRead, RegWrite, MemtoReg, ALUSrc, RegDst}),
    .sel(1'b1));

  // Other names for the same wires on the sheet: addr[11:0] = {op, funct};
  //   ctrl[13:0] = {Syscall, ALUCtl, ZeroExt, Bne, Beq, MemWrite, MemRead, RegWrite, MemtoReg, ALUSrc, RegDst}

  // Notes on the sheet:
  //   contents of rom_1 (hex, n*v repeats v):
  //   12*0 2000 19*0 11 11 411 411 811 c11 4*0 1011 213*0 64*480 64*500 128*0 128*12 192*0 64*e12 64*0
  //   64*18 1216*0 64*36 448*0 64*42
endmodule

module regfile (
  input  [4:0] RR1,
  input  [4:0] RR2,
  input  [4:0] WR,
  input  [31:0] WD,
  input  RegWrite,
  input  clk,
  output [31:0] RD1,
  output [31:0] RD2,
  output [31:0] v0,
  output [31:0] a0
);

  wire we1, we2, we3, we4, we5, we6, we7, we8, we9, we10, we11, we12, we13, we14, we15, we16, we17, we18,
       we19, we20, we21, we22, we23, we24, we25, we26, we27, we28, we29, we30, we31;
  wire [31:0] r1, r3, r5, r6, r7, r8, r9, r10, r11, r12, r13, r14, r15, r16, r17, r18, r19, r20, r21, r22,
       r23, r24, r25, r26, r27, r28, r29, r30, r31;

  Decoder #(.select(5), .disabled(0)) decoder_1 (
    .out1(we1), .out2(we2), .out3(we3), .out4(we4), .out5(we5), .out6(we6), .out7(we7), .out8(we8),
    .out9(we9), .out10(we10), .out11(we11), .out12(we12), .out13(we13), .out14(we14), .out15(we15),
    .out16(we16), .out17(we17), .out18(we18), .out19(we19), .out20(we20), .out21(we21), .out22(we22),
    .out23(we23), .out24(we24), .out25(we25), .out26(we26), .out27(we27), .out28(we28), .out29(we29),
    .out30(we30), .out31(we31), .sel(WR), .en(RegWrite));  // open: out0
  Register #(.width(32)) at (.D(WD), .en(we1), .Q(r1), .clk(clk));  // open: clr
  Register #(.width(32)) u_v0 (.D(WD), .en(we2), .Q(v0), .clk(clk));  // open: clr
  Register #(.width(32)) v1 (.D(WD), .en(we3), .Q(r3), .clk(clk));  // open: clr
  Register #(.width(32)) u_a0 (.D(WD), .en(we4), .Q(a0), .clk(clk));  // open: clr
  Register #(.width(32)) a1 (.D(WD), .en(we5), .Q(r5), .clk(clk));  // open: clr
  Register #(.width(32)) a2 (.D(WD), .en(we6), .Q(r6), .clk(clk));  // open: clr
  Register #(.width(32)) a3 (.D(WD), .en(we7), .Q(r7), .clk(clk));  // open: clr
  Register #(.width(32)) t0 (.D(WD), .en(we8), .Q(r8), .clk(clk));  // open: clr
  Register #(.width(32)) t1 (.D(WD), .en(we9), .Q(r9), .clk(clk));  // open: clr
  Register #(.width(32)) t2 (.D(WD), .en(we10), .Q(r10), .clk(clk));  // open: clr
  Register #(.width(32)) t3 (.D(WD), .en(we11), .Q(r11), .clk(clk));  // open: clr
  Register #(.width(32)) t4 (.D(WD), .en(we12), .Q(r12), .clk(clk));  // open: clr
  Register #(.width(32)) t5 (.D(WD), .en(we13), .Q(r13), .clk(clk));  // open: clr
  Register #(.width(32)) t6 (.D(WD), .en(we14), .Q(r14), .clk(clk));  // open: clr
  Register #(.width(32)) t7 (.D(WD), .en(we15), .Q(r15), .clk(clk));  // open: clr
  Register #(.width(32)) s0 (.D(WD), .en(we16), .Q(r16), .clk(clk));  // open: clr
  Register #(.width(32)) s1 (.D(WD), .en(we17), .Q(r17), .clk(clk));  // open: clr
  Register #(.width(32)) s2 (.D(WD), .en(we18), .Q(r18), .clk(clk));  // open: clr
  Register #(.width(32)) s3 (.D(WD), .en(we19), .Q(r19), .clk(clk));  // open: clr
  Register #(.width(32)) s4 (.D(WD), .en(we20), .Q(r20), .clk(clk));  // open: clr
  Register #(.width(32)) s5 (.D(WD), .en(we21), .Q(r21), .clk(clk));  // open: clr
  Register #(.width(32)) s6 (.D(WD), .en(we22), .Q(r22), .clk(clk));  // open: clr
  Register #(.width(32)) s7 (.D(WD), .en(we23), .Q(r23), .clk(clk));  // open: clr
  Register #(.width(32)) t8 (.D(WD), .en(we24), .Q(r24), .clk(clk));  // open: clr
  Register #(.width(32)) t9 (.D(WD), .en(we25), .Q(r25), .clk(clk));  // open: clr
  Register #(.width(32)) k0 (.D(WD), .en(we26), .Q(r26), .clk(clk));  // open: clr
  Register #(.width(32)) k1 (.D(WD), .en(we27), .Q(r27), .clk(clk));  // open: clr
  Register #(.width(32)) gp (.D(WD), .en(we28), .Q(r28), .clk(clk));  // open: clr
  Register #(.width(32)) sp (.D(WD), .en(we29), .Q(r29), .clk(clk));  // open: clr
  Register #(.width(32)) fp (.D(WD), .en(we30), .Q(r30), .clk(clk));  // open: clr
  Register #(.width(32)) ra (.D(WD), .en(we31), .Q(r31), .clk(clk));  // open: clr
  Multiplexer #(.select(5), .width(32), .enable("false")) multiplexer_1 (
    .in0({32{1'b0}}), .in1(r1), .in2(v0), .in3(r3), .in4(a0), .in5(r5), .in6(r6), .in7(r7), .in8(r8),
    .in9(r9), .in10(r10), .in11(r11), .in12(r12), .in13(r13), .in14(r14), .in15(r15), .in16(r16), .in17(r17),
    .in18(r18), .in19(r19), .in20(r20), .in21(r21), .in22(r22), .in23(r23), .in24(r24), .in25(r25),
    .in26(r26), .in27(r27), .in28(r28), .in29(r29), .in30(r30), .in31(r31), .out(RD1), .sel(RR1));
  Multiplexer #(.select(5), .width(32), .enable("false")) multiplexer_2 (
    .in0({32{1'b0}}), .in1(r1), .in2(v0), .in3(r3), .in4(a0), .in5(r5), .in6(r6), .in7(r7), .in8(r8),
    .in9(r9), .in10(r10), .in11(r11), .in12(r12), .in13(r13), .in14(r14), .in15(r15), .in16(r16), .in17(r17),
    .in18(r18), .in19(r19), .in20(r20), .in21(r21), .in22(r22), .in23(r23), .in24(r24), .in25(r25),
    .in26(r26), .in27(r27), .in28(r28), .in29(r29), .in30(r30), .in31(r31), .out(RD2), .sel(RR2));

  // Other names for the same wires on the sheet: r2[31:0] = v0; r4[31:0] = a0
endmodule

module alu (
  input  [31:0] A,
  input  [31:0] B,
  input  [2:0] ALUCtl,
  output [31:0] Result,
  output Zero
);

  wire ltBit;
  wire [31:0] andv, diff, orv, sltv, sum;

  Adder #(.width(32)) adder_1 (.a(A), .b(B), .out(sum));  // open: cin, cout
  Subtractor #(.width(32)) subtractor_1 (.a(A), .b(B), .out(diff));  // open: bin, bout
  assign andv = A & B;  // AND_Gate and_1, 32 bits wide
  assign orv = A | B;  // OR_Gate or_1, 32 bits wide
  Comparator #(.width(32)) comparator_1 (.a(A), .b(B), .lt(ltBit));  // open: gt, eq
  assign sltv = {{31{1'b0}}, ltBit};  // Bit_Extender bit_extender_1
  Multiplexer #(.select(3), .width(32), .enable("false")) multiplexer_1 (
    .in0(sum), .in1(diff), .in2(andv), .in3(orv), .in4(sltv), .in5({32{1'b0}}), .in6({32{1'b0}}),
    .in7({32{1'b0}}), .out(Result), .sel(ALUCtl));
  Comparator #(.width(32)) comparator_2 (.a(Result), .b({32{1'b0}}), .eq(Zero));  // open: gt, lt
endmodule
